# Fritzing sketch robo tx demo (saved by Fritzing 0.8.7b)
breadboards: 1

parts:
  VCC1 = Battery block 9V
  Bauteil1 = fischertechnik ROBO TX
  M1 = DC Motor
  M2 = DC Motor
  R1 = Rotary Potentiometer (Small) [maximum_resistance=10kΩ package=THT]
  R2 = Photocell (LDR) [package=THT]
  LED1 = LED - 5mm [color="Red (633nm)" package="5 mm [THT]"]
  LED2 = LED - 5mm [color="Green (555nm)" package="5 mm [THT]"]
  R3 = Resistor [tolerance=±5% resistance=680k package=THT]
  R4 = Resistor [tolerance=±5% resistance=680 package=THT]
  U1 = DS1307 [package=so08]
  S1 = Round Pushbutton  # not connected

nets:
  N1: VCC1.-, Bauteil1.9VIn_GND
  N2: VCC1.+, Bauteil1.9VIn+
  N3: Bauteil1.I1, R1.wiper
  N4: Bauteil1.I5, R2.pin_0
  N5: Bauteil1.GND_I1, R1.leg1
  N6: Bauteil1.GND_I5, R2.pin_1
  N7: Bauteil1.M1_O1, M1.pin_1
  N8: Bauteil1.M2_O1, M2.pin_1
  N9: Bauteil1.M3_O1, LED1.cathode
  N10: Bauteil1.M1_O2, M1.pin_2
  N11: Bauteil1.M2_O2, M2.pin_2
  N12: Bauteil1.M3_O2, LED2.cathode
  N13: Bauteil1.GND_C4, R3.Pin_1, R4.Pin_1, U1.GND
  N14: Bauteil1.9V0ut+, R1.leg2
  N15: Bauteil1.EXT2_I2C_Clock, U1.SCL
  N16: Bauteil1.EXT2_I2C_Data, U1.SDA
  N17: Bauteil1.EXT2_5_Volt_Out_+, U1.VCC
  N18: LED1.anode, R3.Pin_0
  N19: LED2.anode, R4.Pin_0

custom parts:
  fischertechnik ROBO TX: fischertechnik ROBO TX Controller I1 ... I8 Universal inputs: Digital, analog 0-9V DC, analog 0-5kΩ C1 ... C4 fast counting inputs: Digital, frequency up to 1kHz M1 .. M4 4 motor outputs, 9V, 250mA: Speed infinitely variable, short circuit proof, alternatively 8 individual outputs EXT1 RS 485 for coupling of additional „ROBOTX Controller“ EXT2 I2C Size: 90x90x15mm
